// Logisim project mips_pipeline.circ as structural Verilog: 13 circuits, main circuit main
module main (
);

  wire and_1_out, and_2_out, and_3_out, and_4_out, and_5_out, and_6_out, and_7_out, and_8_out, and_9_out,
       and_10_out, and_11_out, and_12_out, button_1_out, clock_1_out, fowarding_1_fsw, hazard_unit_1_stall,
       not_1_out, not_2_out, reg_ex_mem_1_beq_2, reg_ex_mem_1_bne_2, reg_ex_mem_1_jal_2, reg_ex_mem_1_jr_2,
       reg_ex_mem_1_jump_2, reg_ex_mem_1_memory_write_2, reg_ex_mem_1_memtoreg_2, reg_ex_mem_1_regwrite_2,
       reg_ex_mem_1_zero_2, reg_id_ex_1_alusrc_2, reg_id_ex_1_bne_2, reg_id_ex_1_branch, reg_id_ex_1_jal_2,
       reg_id_ex_1_jr_2, reg_id_ex_1_jump_4, reg_id_ex_1_memtoreg_2, reg_id_ex_1_memwrite_2,
       reg_id_ex_1_regdest_2, reg_id_ex_1_regwrite_2, reg_mem_wb_1_jal_2, reg_mem_wb_1_memtoreg_2,
       reg_mem_wb_1_reg_write_2, uc_w_1_alusrc, uc_w_1_beq, uc_w_1_bne, uc_w_1_jal, uc_w_1_jr, uc_w_1_jump,
       uc_w_1_memtoreg, uc_w_1_memwrite, uc_w_1_regdest, uc_w_1_regwrite, ula_1_igual;
  wire [1:0] fowarding_1_fa, fowarding_1_fb, or_1_out;
  wire [3:0] reg_id_ex_1_aluop_2, uc_w_1_aluop;
  wire [4:0] id_ex_RT, if_id_RS, if_id_RT, multiplexer_2_out, multiplexer_4_out, reg_ex_mem_1_rt_2,
       reg_ex_mem_1_write_register_2, reg_id_ex_1_rd_2, reg_id_ex_1_rs_2, reg_id_ex_1_shamt_2,
       reg_mem_wb_1_write_register_2;
  wire [5:0] alu_control_1_out_3, reg_if_id_1_out_6_2;
  wire [15:0] reg_if_id_1_out_6;
  wire [25:0] reg_id_ex_1_jump_3, shifter_1_out;
  wire [31:0] adder_1_out, adder_2_out, banco_registradores_1_r1, banco_registradores_1_r2,
       bit_extender_1_out, data1, data2, ex_memdata, multiplexer_1_out, multiplexer_3_out, multiplexer_5_out,
       multiplexer_8_out, multiplexer_9_out, PC_q, ram_1_data, ram_2_data, reg_ex_mem_1_br_rs_2,
       reg_ex_mem_1_branch_address_2, reg_ex_mem_1_data_rt_2, reg_ex_mem_1_jump_address_2,
       reg_ex_mem_1_jump_address_3, reg_id_ex_1_imext_2, reg_id_ex_1_pc_4_2, reg_if_id_1_out_5,
       reg_mem_wb_1_alu_out_2, reg_mem_wb_1_mem_out_2, reg_mem_wb_1_pc_4_2, rsdata, rtdata, shifter_2_out,
       ula_1_resultado;

  not not_1 (not_1_out, hazard_unit_1_stall);
  Multiplexer #(.select(2), .width(32), .enable("false")) multiplexer_1 (
    .in0(adder_1_out), .in1(reg_ex_mem_1_jump_address_3), .in2(reg_ex_mem_1_branch_address_2),
    .in3(reg_ex_mem_1_br_rs_2), .out(multiplexer_1_out), .sel(or_1_out));
  Adder #(.width(32)) adder_1 (.a(32'h4), .b(PC_q), .out(adder_1_out));  // open: cin, cout
  Register #(.width(32)) PC (.D(multiplexer_1_out), .en(not_1_out), .Q(PC_q), .clk(clock_1_out), .clr(button_1_out));
  Button button_1 (.out(button_1_out));
  RAM #(.addrWidth(16), .dataWidth(32)) ram_1 (
    .addr(PC_q[17:2]), .data(ram_1_data), .clk(clock_1_out));  // open: sel, ld, clr
  hazard_unit hazard_unit_1 (
    .id_ex_readmem(reg_id_ex_1_memtoreg_2), .id_ex_regRt(id_ex_RT), .if_id_regRs(if_id_RS),
    .if_id_regRt(if_id_RT), .opcode(reg_if_id_1_out_6_2), .stall(hazard_unit_1_stall));
  REG_IF_ID reg_if_id_1 (
    .in_2(adder_1_out), .in_3(ram_1_data), .out_5(reg_if_id_1_out_5),
    .out_6({reg_if_id_1_out_6_2, if_id_RS, if_id_RT, reg_if_id_1_out_6}), .CLK(clock_1_out),
    .stall(hazard_unit_1_stall));
  UC_W uc_w_1 (
    .in_1(reg_if_id_1_out_6_2), .REGDEST(uc_w_1_regdest), .JUMP(uc_w_1_jump), .BEQ(uc_w_1_beq),
    .MEMTOREG(uc_w_1_memtoreg), .ALUOP(uc_w_1_aluop), .MEMWRITE(uc_w_1_memwrite), .ALUSRC(uc_w_1_alusrc),
    .REGWRITE(uc_w_1_regwrite), .BNE(uc_w_1_bne), .JR(uc_w_1_jr), .JAL(uc_w_1_jal));
  Multiplexer #(.width(5), .enable("false")) multiplexer_2 (
    .in0(reg_mem_wb_1_write_register_2), .in1({5{1'b1}}), .out(multiplexer_2_out), .sel(reg_mem_wb_1_jal_2));
  Multiplexer #(.width(32), .enable("false")) multiplexer_3 (
    .in0(multiplexer_9_out), .in1(reg_mem_wb_1_pc_4_2), .out(multiplexer_3_out), .sel(reg_mem_wb_1_jal_2));
  banco_registradores banco_registradores_1 (
    .R1_num(if_id_RS), .R2_num(if_id_RT), .RW(multiplexer_2_out), .Din(multiplexer_3_out),
    .WE(reg_mem_wb_1_reg_write_2), .clk(clock_1_out), .R1(banco_registradores_1_r1),
    .R2(banco_registradores_1_r2));
  assign bit_extender_1_out = {{16{reg_if_id_1_out_6[15]}}, reg_if_id_1_out_6};  // Bit_Extender bit_extender_1
  Clock clock_1 (.out(clock_1_out));
  and and_1 (and_1_out, ~hazard_unit_1_stall, uc_w_1_alusrc);  // AND_Gate
  and and_2 (and_2_out, ~hazard_unit_1_stall, uc_w_1_regwrite);  // AND_Gate
  and and_3 (and_3_out, ~hazard_unit_1_stall, uc_w_1_bne);  // AND_Gate
  and and_4 (and_4_out, ~hazard_unit_1_stall, uc_w_1_jr);  // AND_Gate
  and and_5 (and_5_out, ~hazard_unit_1_stall, uc_w_1_jal);  // AND_Gate
  REG_ID_EX reg_id_ex_1 (
    .RegDest(and_6_out), .BEQ(and_8_out), .MemtoReg(and_9_out), .ALUOp(uc_w_1_aluop), .ALUSrc(and_1_out),
    .RegWrite(and_2_out), .PC_4(reg_if_id_1_out_5), .DATA_RS(banco_registradores_1_r1),
    .DATA_RT(banco_registradores_1_r2), .IMEXT(bit_extender_1_out), .RT(if_id_RT),
    .RD(reg_if_id_1_out_6[15:11]), .RegDest_2(reg_id_ex_1_regdest_2), .Branch(reg_id_ex_1_branch),
    .MemtoReg_2(reg_id_ex_1_memtoreg_2), .ALUOp_2(reg_id_ex_1_aluop_2), .ALUSrc_2(reg_id_ex_1_alusrc_2),
    .RegWrite_2(reg_id_ex_1_regwrite_2), .PC_4_2(reg_id_ex_1_pc_4_2), .DATA_RS_2(rsdata), .DATA_RT_2(rtdata),
    .IMEXT_2(reg_id_ex_1_imext_2), .RT_2(id_ex_RT), .RD_2(reg_id_ex_1_rd_2), .CLK(clock_1_out),
    .MemWrite(and_10_out), .MemWrite_2(reg_id_ex_1_memwrite_2), .SHAMT(reg_if_id_1_out_6[10:6]),
    .SHAMT_2(reg_id_ex_1_shamt_2), .JUMP_2(and_7_out), .JUMP_4(reg_id_ex_1_jump_4),
    .JUMP({if_id_RS, if_id_RT, reg_if_id_1_out_6}), .JUMP_3(reg_id_ex_1_jump_3), .BNE_2(reg_id_ex_1_bne_2),
    .BNE(and_3_out), .JR(and_4_out), .JAL(and_5_out), .JR_2(reg_id_ex_1_jr_2), .JAL_2(reg_id_ex_1_jal_2),
    .RS(if_id_RS), .RS_2(reg_id_ex_1_rs_2));
  and and_6 (and_6_out, ~hazard_unit_1_stall, uc_w_1_regdest);  // AND_Gate
  and and_7 (and_7_out, ~hazard_unit_1_stall, uc_w_1_jump);  // AND_Gate
  and and_8 (and_8_out, ~hazard_unit_1_stall, uc_w_1_beq);  // AND_Gate
  and and_9 (and_9_out, ~hazard_unit_1_stall, uc_w_1_memtoreg);  // AND_Gate
  and and_10 (and_10_out, ~hazard_unit_1_stall, uc_w_1_memwrite);  // AND_Gate
  Multiplexer #(.width(5), .enable("false")) multiplexer_4 (
    .in0(id_ex_RT), .in1(reg_id_ex_1_rd_2), .out(multiplexer_4_out), .sel(reg_id_ex_1_regdest_2));
  Shifter #(.width(26)) shifter_1 (.in(reg_id_ex_1_jump_3), .\dist (5'b00010), .out(shifter_1_out));
  Shifter #(.width(32)) shifter_2 (.in(reg_id_ex_1_imext_2), .\dist (5'b00010), .out(shifter_2_out));
  ULA ula_1 (
    .A(data1), .B(multiplexer_5_out), .Resultado(ula_1_resultado), .OP(alu_control_1_out_3),
    .igual(ula_1_igual), .SHAMT(reg_id_ex_1_shamt_2));
  Multiplexer #(.width(32), .enable("false")) multiplexer_5 (
    .in0(data2), .in1(reg_id_ex_1_imext_2), .out(multiplexer_5_out), .sel(reg_id_ex_1_alusrc_2));
  ALU_CONTROL alu_control_1 (.in_1(reg_id_ex_1_imext_2[5:0]), .out_3(alu_control_1_out_3), .in_2(reg_id_ex_1_aluop_2));
  Multiplexer #(.select(2), .width(32), .enable("false")) multiplexer_6 (
    .in0(rsdata), .in1(multiplexer_9_out), .in2(ex_memdata), .out(data1), .sel(fowarding_1_fa));  // open: in3
  Multiplexer #(.select(2), .width(32), .enable("false")) multiplexer_7 (
    .in0(rtdata), .in1(multiplexer_9_out), .in2(ex_memdata), .out(data2), .sel(fowarding_1_fb));  // open: in3
  Adder #(.width(32)) adder_2 (.a(reg_id_ex_1_pc_4_2), .b(shifter_2_out), .out(adder_2_out));  // open: cin, cout
  REG_EX_MEM reg_ex_mem_1 (
    .BEQ(reg_id_ex_1_branch), .MEMTOREG(reg_id_ex_1_memtoreg_2), .MEMORY_WRITE(reg_id_ex_1_memwrite_2),
    .REGWRITE(reg_id_ex_1_regwrite_2), .BRANCH_ADDRESS(adder_2_out), .zero(ula_1_igual),
    .ALU_OUT(ula_1_resultado), .DATA_RT(rtdata), .WRITE_REGISTER(multiplexer_4_out),
    .BEQ_2(reg_ex_mem_1_beq_2), .MEMTOREG_2(reg_ex_mem_1_memtoreg_2),
    .MEMORY_WRITE_2(reg_ex_mem_1_memory_write_2), .REGWRITE_2(reg_ex_mem_1_regwrite_2),
    .BRANCH_ADDRESS_2(reg_ex_mem_1_branch_address_2), .zero_2(reg_ex_mem_1_zero_2), .ALU_OUT_2(ex_memdata),
    .DATA_RT_2(reg_ex_mem_1_data_rt_2), .WRITE_REGISTER_2(reg_ex_mem_1_write_register_2), .CLK(clock_1_out),
    .JUMP_ADDRESS({reg_id_ex_1_pc_4_2[31:28], shifter_1_out, 2'b00}),
    .JUMP_ADDRESS_3(reg_ex_mem_1_jump_address_3), .JUMP(reg_id_ex_1_jump_4), .JUMP_2(reg_ex_mem_1_jump_2),
    .BNE(reg_id_ex_1_bne_2), .BNE_2(reg_ex_mem_1_bne_2), .JR(reg_id_ex_1_jr_2), .JAL(reg_id_ex_1_jal_2),
    .JR_2(reg_ex_mem_1_jr_2), .JAL_2(reg_ex_mem_1_jal_2), .PC_4(reg_id_ex_1_pc_4_2),
    .JUMP_ADDRESS_2(reg_ex_mem_1_jump_address_2), .BR_RS(rtdata), .BR_RS_2(reg_ex_mem_1_br_rs_2),
    .RT(id_ex_RT), .RT_2(reg_ex_mem_1_rt_2));
  or or_1 (or_1_out[0], reg_ex_mem_1_jump_2, reg_ex_mem_1_jal_2, reg_ex_mem_1_jr_2);
  and and_11 (and_11_out, reg_ex_mem_1_zero_2, reg_ex_mem_1_beq_2);
  Multiplexer #(.width(32), .enable("false")) multiplexer_8 (
    .in0(reg_ex_mem_1_data_rt_2), .in1(multiplexer_9_out), .out(multiplexer_8_out), .sel(fowarding_1_fsw));
  or or_2 (or_1_out[1], reg_ex_mem_1_jr_2, and_11_out, and_12_out);
  and and_12 (and_12_out, not_2_out, reg_ex_mem_1_bne_2);
  not not_2 (not_2_out, reg_ex_mem_1_zero_2);
  fowarding fowarding_1 (
    .ex_mem_writeReg(reg_ex_mem_1_regwrite_2), .ex_mem_RegDd(reg_ex_mem_1_write_register_2),
    .id_ex_RegRs(reg_id_ex_1_rs_2), .ex_mem_RegRt(reg_ex_mem_1_rt_2),
    .mem_wb_writeReg(reg_mem_wb_1_reg_write_2), .mem_wb_RegDd(reg_mem_wb_1_write_register_2),
    .id_ex_RegRt(id_ex_RT), .FA(fowarding_1_fa), .fsw(fowarding_1_fsw), .FB(fowarding_1_fb));
  RAM #(.addrWidth(16), .dataWidth(32), .bus("separate")) ram_2 (
    .addr(ex_memdata[17:2]), .din(multiplexer_8_out), .data(ram_2_data), .str(reg_ex_mem_1_memory_write_2),
    .clk(clock_1_out));  // open: sel, ld, clr
  REG_MEM_WB reg_mem_wb_1 (
    .REG_WRITE(reg_ex_mem_1_regwrite_2), .MEMTOREG(reg_ex_mem_1_memtoreg_2), .MEM_OUT(ram_2_data),
    .ALU_OUT(ex_memdata), .WRITE_REGISTER(reg_ex_mem_1_write_register_2),
    .REG_WRITE_2(reg_mem_wb_1_reg_write_2), .MEMTOREG_2(reg_mem_wb_1_memtoreg_2),
    .MEM_OUT_2(reg_mem_wb_1_mem_out_2), .ALU_OUT_2(reg_mem_wb_1_alu_out_2),
    .WRITE_REGISTER_2(reg_mem_wb_1_write_register_2), .CLK(clock_1_out), .PC_4(reg_ex_mem_1_jump_address_2),
    .PC_4_2(reg_mem_wb_1_pc_4_2), .JAL(reg_ex_mem_1_jal_2), .JAL_2(reg_mem_wb_1_jal_2));
  Multiplexer #(.width(32), .enable("false")) multiplexer_9 (
    .in0(reg_mem_wb_1_alu_out_2), .in1(reg_mem_wb_1_mem_out_2), .out(multiplexer_9_out),
    .sel(reg_mem_wb_1_memtoreg_2));

  // Notes on the sheet:
  //   RegDest
  //   Jump
  //   BEQ
  //   MemtoReg
  //   ALUOp
  //   MemWrite
  //   ALUSrc
  //   RegWrite
  //   BNE
  //   JR
  //   JAL
endmodule

module banco_registradores (
  input  [4:0] R1_num,
  input  [4:0] R2_num,
  input  [4:0] RW,
  input  [31:0] Din,
  input  WE,
  input  clk,
  output [31:0] R1,
  output [31:0] R2
);

  wire and_1_out, and_2_out, comparator_1_eq, comparator_2_eq, demultiplexer_1_out0, demultiplexer_1_out1,
       demultiplexer_1_out2, demultiplexer_1_out3, demultiplexer_2_out0, demultiplexer_2_out1,
       demultiplexer_2_out2, demultiplexer_2_out3, demultiplexer_2_out4, demultiplexer_2_out5,
       demultiplexer_2_out6, demultiplexer_2_out7, demultiplexer_3_out0, demultiplexer_3_out1,
       demultiplexer_3_out2, demultiplexer_3_out3, demultiplexer_3_out4, demultiplexer_3_out5,
       demultiplexer_3_out6, demultiplexer_3_out7, demultiplexer_4_out0, demultiplexer_4_out1,
       demultiplexer_4_out2, demultiplexer_4_out3, demultiplexer_4_out4, demultiplexer_4_out5,
       demultiplexer_4_out6, demultiplexer_4_out7, demultiplexer_5_out0, demultiplexer_5_out1,
       demultiplexer_5_out2, demultiplexer_5_out3, demultiplexer_5_out4, demultiplexer_5_out5,
       demultiplexer_5_out6, demultiplexer_5_out7;
  wire [31:0] _0__Zero_q, _1__at_q, _3__v1_q, _5__a1_q, _6__a2_q, _7__a3_q, _8__t0_q, _9__t1_q, _10__t2_q,
       _11__t3_q, _12__t4_q, _13__t5_q, _14__t6_q, _15__t7_q, _19__s3_q, _20__s4_q, _21__s5_q, _22__s6_q,
       _23__s7_q, _24__t8_q, _25__t9_q, _26__k0_q, _27__k1_q, _28__gp_q, _29__sp_q, _30__fp_q, a0,
       multiplexer_2_out, multiplexer_3_out, ra, s0, s1, s2, v0;

  Demultiplexer #(.select(2), .disabled(0)) demultiplexer_1 (
    .out0(demultiplexer_1_out0), .out1(demultiplexer_1_out1), .out2(demultiplexer_1_out2),
    .out3(demultiplexer_1_out3), .in(1'b1), .sel(RW[4:3]), .en(WE));
  Demultiplexer #(.select(3), .disabled(0)) demultiplexer_2 (
    .out0(demultiplexer_2_out0), .out1(demultiplexer_2_out1), .out2(demultiplexer_2_out2),
    .out3(demultiplexer_2_out3), .out4(demultiplexer_2_out4), .out5(demultiplexer_2_out5),
    .out6(demultiplexer_2_out6), .out7(demultiplexer_2_out7), .in(1'b1), .sel(RW[2:0]),
    .en(demultiplexer_1_out0));
  Demultiplexer #(.select(3), .disabled(0)) demultiplexer_3 (
    .out0(demultiplexer_3_out0), .out1(demultiplexer_3_out1), .out2(demultiplexer_3_out2),
    .out3(demultiplexer_3_out3), .out4(demultiplexer_3_out4), .out5(demultiplexer_3_out5),
    .out6(demultiplexer_3_out6), .out7(demultiplexer_3_out7), .in(1'b1), .sel(RW[2:0]),
    .en(demultiplexer_1_out1));
  Demultiplexer #(.select(3), .disabled(0)) demultiplexer_4 (
    .out0(demultiplexer_4_out0), .out1(demultiplexer_4_out1), .out2(demultiplexer_4_out2),
    .out3(demultiplexer_4_out3), .out4(demultiplexer_4_out4), .out5(demultiplexer_4_out5),
    .out6(demultiplexer_4_out6), .out7(demultiplexer_4_out7), .in(1'b1), .sel(RW[2:0]),
    .en(demultiplexer_1_out2));
  Demultiplexer #(.select(3), .disabled(0)) demultiplexer_5 (
    .out0(demultiplexer_5_out0), .out1(demultiplexer_5_out1), .out2(demultiplexer_5_out2),
    .out3(demultiplexer_5_out3), .out4(demultiplexer_5_out4), .out5(demultiplexer_5_out5),
    .out6(demultiplexer_5_out6), .out7(demultiplexer_5_out7), .in(1'b1), .sel(RW[2:0]),
    .en(demultiplexer_1_out3));
  Register #(.width(32)) _0__Zero (.D(Din), .en(demultiplexer_2_out0), .Q(_0__Zero_q));  // open: clk, clr
  Register #(.width(32)) _8__t0 (.D(Din), .en(demultiplexer_3_out0), .Q(_8__t0_q), .clk(clk));  // open: clr
  Register #(.width(32)) _16__s0 (.D(Din), .en(demultiplexer_4_out0), .Q(s0), .clk(clk));  // open: clr
  Register #(.width(32)) _24__t8 (.D(Din), .en(demultiplexer_5_out0), .Q(_24__t8_q), .clk(clk));  // open: clr
  Register #(.width(32)) _1__at (.D(Din), .en(demultiplexer_2_out1), .Q(_1__at_q), .clk(clk));  // open: clr
  Register #(.width(32)) _9__t1 (.D(Din), .en(demultiplexer_3_out1), .Q(_9__t1_q), .clk(clk));  // open: clr
  Register #(.width(32)) _17__s1 (.D(Din), .en(demultiplexer_4_out1), .Q(s1), .clk(clk));  // open: clr
  Register #(.width(32)) _25__t9 (.D(Din), .en(demultiplexer_5_out1), .Q(_25__t9_q), .clk(clk));  // open: clr
  Register #(.width(32)) _2__v0 (.D(Din), .en(demultiplexer_2_out2), .Q(v0), .clk(clk));  // open: clr
  Register #(.width(32)) _10__t2 (.D(Din), .en(demultiplexer_3_out2), .Q(_10__t2_q), .clk(clk));  // open: clr
  Register #(.width(32)) _18__s2 (.D(Din), .en(demultiplexer_4_out2), .Q(s2), .clk(clk));  // open: clr
  Register #(.width(32)) _26__k0 (.D(Din), .en(demultiplexer_5_out2), .Q(_26__k0_q), .clk(clk));  // open: clr
  Register #(.width(32)) _3__v1 (.D(Din), .en(demultiplexer_2_out3), .Q(_3__v1_q), .clk(clk));  // open: clr
  Register #(.width(32)) _11__t3 (.D(Din), .en(demultiplexer_3_out3), .Q(_11__t3_q), .clk(clk));  // open: clr
  Register #(.width(32)) _19__s3 (.D(Din), .en(demultiplexer_4_out3), .Q(_19__s3_q), .clk(clk));  // open: clr
  Register #(.width(32)) _27__k1 (.D(Din), .en(demultiplexer_5_out3), .Q(_27__k1_q), .clk(clk));  // open: clr
  Register #(.width(32)) _4__a0 (.D(Din), .en(demultiplexer_2_out4), .Q(a0), .clk(clk));  // open: clr
  Register #(.width(32)) _12__t4 (.D(Din), .en(demultiplexer_3_out4), .Q(_12__t4_q), .clk(clk));  // open: clr
  Register #(.width(32)) _20__s4 (.D(Din), .en(demultiplexer_4_out4), .Q(_20__s4_q), .clk(clk));  // open: clr
  Register #(.width(32)) _28__gp (.D(Din), .en(demultiplexer_5_out4), .Q(_28__gp_q), .clk(clk));  // open: clr
  Register #(.width(32)) _5__a1 (.D(Din), .en(demultiplexer_2_out5), .Q(_5__a1_q), .clk(clk));  // open: clr
  Register #(.width(32)) _13__t5 (.D(Din), .en(demultiplexer_3_out5), .Q(_13__t5_q), .clk(clk));  // open: clr
  Register #(.width(32)) _21__s5 (.D(Din), .en(demultiplexer_4_out5), .Q(_21__s5_q), .clk(clk));  // open: clr
  Register #(.width(32)) _29__sp (.D(Din), .en(demultiplexer_5_out5), .Q(_29__sp_q), .clk(clk));  // open: clr
  Register #(.width(32)) _6__a2 (.D(Din), .en(demultiplexer_2_out6), .Q(_6__a2_q), .clk(clk));  // open: clr
  Register #(.width(32)) _14__t6 (.D(Din), .en(demultiplexer_3_out6), .Q(_14__t6_q), .clk(clk));  // open: clr
  Register #(.width(32)) _22__s6 (.D(Din), .en(demultiplexer_4_out6), .Q(_22__s6_q), .clk(clk));  // open: clr
  Register #(.width(32)) _30__fp (.D(Din), .en(demultiplexer_5_out6), .Q(_30__fp_q), .clk(clk));  // open: clr
  Register #(.width(32)) _7__a3 (.D(Din), .en(demultiplexer_2_out7), .Q(_7__a3_q), .clk(clk));  // open: clr
  Register #(.width(32)) _15__t7 (.D(Din), .en(demultiplexer_3_out7), .Q(_15__t7_q), .clk(clk));  // open: clr
  Register #(.width(32)) _23__s7 (.D(Din), .en(demultiplexer_4_out7), .Q(_23__s7_q), .clk(clk));  // open: clr
  Register #(.width(32)) _31__ra (.D(Din), .en(demultiplexer_5_out7), .Q(ra), .clk(clk));  // open: clr
  Comparator #(.width(5), .mode("unsigned")) comparator_1 (.a(RW), .b(R1_num), .eq(comparator_1_eq));  // open: gt, lt
  Comparator #(.width(5), .mode("unsigned")) comparator_2 (.a(RW), .b(R2_num), .eq(comparator_2_eq));  // open: gt, lt
  Multiplexer #(.width(32), .enable("false")) multiplexer_1 (
    .in0(multiplexer_2_out), .in1(Din), .out(R1), .sel(and_1_out));
  and and_1 (and_1_out, comparator_1_eq, WE);
  Multiplexer #(.select(5), .width(32), .enable("false")) multiplexer_2 (
    .in0(_0__Zero_q), .in1(_1__at_q), .in2(v0), .in3(_3__v1_q), .in4(a0), .in5(_5__a1_q), .in6(_6__a2_q),
    .in7(_7__a3_q), .in8(_8__t0_q), .in9(_9__t1_q), .in10(_10__t2_q), .in11(_11__t3_q), .in12(_12__t4_q),
    .in13(_13__t5_q), .in14(_14__t6_q), .in15(_15__t7_q), .in16(s0), .in17(s1), .in18(s2), .in19(_19__s3_q),
    .in20(_20__s4_q), .in21(_21__s5_q), .in22(_22__s6_q), .in23(_23__s7_q), .in24(_24__t8_q),
    .in25(_25__t9_q), .in26(_26__k0_q), .in27(_27__k1_q), .in28(_28__gp_q), .in29(_29__sp_q),
    .in30(_30__fp_q), .in31(ra), .out(multiplexer_2_out), .sel(R1_num));
  Multiplexer #(.select(5), .width(32), .enable("false")) multiplexer_3 (
    .in0(_0__Zero_q), .in1(_1__at_q), .in2(v0), .in3(_3__v1_q), .in4(a0), .in5(_5__a1_q), .in6(_6__a2_q),
    .in7(_7__a3_q), .in8(_8__t0_q), .in9(_9__t1_q), .in10(_10__t2_q), .in11(_11__t3_q), .in12(_12__t4_q),
    .in13(_13__t5_q), .in14(_14__t6_q), .in15(_15__t7_q), .in16(s0), .in17(s1), .in18(s2), .in19(_19__s3_q),
    .in20(_20__s4_q), .in21(_21__s5_q), .in22(_22__s6_q), .in23(_23__s7_q), .in24(_24__t8_q),
    .in25(_25__t9_q), .in26(_26__k0_q), .in27(_27__k1_q), .in28(_28__gp_q), .in29(_29__sp_q),
    .in30(_30__fp_q), .in31(ra), .out(multiplexer_3_out), .sel(R2_num));
  Multiplexer #(.width(32), .enable("false")) multiplexer_4 (
    .in0(multiplexer_3_out), .in1(Din), .out(R2), .sel(and_2_out));
  and and_2 (and_2_out, comparator_2_eq, WE);

  // Other names for the same wires on the sheet: reg1[31:0] = R1; reg1_num[4:0] = R1_num; reg2[31:0] = R2;
  //   reg2_num[4:0] = R2_num; write_data[31:0] = Din; write_reg_num[4:0] = RW

  // Notes on the sheet:
  //   Input
  //   Output
endmodule

module ULA (
  input  [31:0] A,
  input  [31:0] B,
  input  [5:0] OP,
  input  [4:0] SHAMT,
  output igual,
  output [31:0] Resultado
);

  wire comparator_1_lt;
  wire [31:0] adder_1_out, and_1_out, bit_extender_1_out, divider_1_out, multiplier_1_out, or_1_out,
       shifter_1_out, shifter_2_out, subtractor_1_out;

  Adder #(.width(32)) adder_1 (.a(A), .b(B), .out(adder_1_out));  // open: cin, cout
  Subtractor #(.width(32)) subtractor_1 (.a(A), .b(B), .out(subtractor_1_out));  // open: bin, bout
  Multiplier #(.width(32)) multiplier_1 (.a(A), .b(B), .out(multiplier_1_out));  // open: cin, cout
  Divider #(.width(32)) divider_1 (.a(A), .b(B), .out(divider_1_out));  // open: upper, rem
  assign and_1_out = A & B;  // AND_Gate and_1, 32 bits wide
  assign or_1_out = A | B;  // OR_Gate or_1, 32 bits wide
  Comparator #(.width(32)) comparator_1 (.a(A), .b(B), .eq(igual), .lt(comparator_1_lt));  // open: gt
  Shifter #(.width(32)) shifter_1 (.in(A), .\dist (SHAMT), .out(shifter_1_out));
  Shifter #(.width(32), .shift("lr")) shifter_2 (.in(A), .\dist (SHAMT), .out(shifter_2_out));
  assign bit_extender_1_out = {{31{1'b0}}, comparator_1_lt};  // Bit_Extender bit_extender_1
  Multiplexer #(.select(4), .width(32), .enable("false")) multiplexer_1 (
    .in0(adder_1_out), .in1(subtractor_1_out), .in2(multiplier_1_out), .in3(divider_1_out), .in4(and_1_out),
    .in5(or_1_out), .in6(bit_extender_1_out), .in7(shifter_1_out), .in8(shifter_2_out), .out(Resultado),
    .sel(OP[3:0]));  // open: in9, in10, in11, in12, in13, in14, in15
endmodule

module UC (
  input  UC5,
  input  UC4,
  input  UC3,
  input  UC2,
  input  UC1,
  input  UC0,
  output REGDEST,
  output JUMP,
  output BEQ,
  output MEMTOREG,
  output ULA0P0,
  output ULA0P1,
  output ULA0P2,
  output ULAOPSRC,
  output MEM_WR,
  output ULASRC,
  output BNE,
  output JR,
  output JAL,
  output WE
);

  wire and_5_out, and_6_out, and_7_out, and_8_out, and_9_out, and_10_out, and_11_out, and_12_out, and_13_out,
       and_14_out, and_16_out, and_17_out, and_18_out, and_19_out, and_20_out, and_22_out, and_23_out,
       and_24_out, and_25_out, and_26_out, and_30_out, and_31_out, and_32_out, and_33_out, not_1_out,
       not_2_out, not_3_out, not_4_out, not_5_out, not_6_out, not_7_out, not_8_out, not_9_out, not_10_out,
       not_11_out, not_12_out, not_13_out, not_14_out, not_15_out, not_16_out, not_17_out, not_18_out,
       not_19_out, not_20_out, not_21_out, not_22_out, not_23_out, not_24_out, not_25_out, not_26_out,
       not_27_out, not_28_out, not_29_out, not_30_out, not_31_out, not_32_out, not_33_out, not_34_out,
       not_35_out, not_36_out, not_37_out, not_38_out, not_39_out, not_40_out, not_41_out, not_42_out,
       not_43_out, not_44_out, not_45_out, not_46_out, not_47_out, not_48_out, not_49_out, not_50_out,
       not_51_out, not_52_out, not_53_out, not_54_out, not_55_out, not_56_out, not_57_out, not_58_out,
       not_59_out, not_60_out, not_61_out, not_62_out, not_63_out, not_64_out, not_65_out, not_66_out,
       not_67_out, not_68_out, not_69_out, not_70_out, not_71_out, not_72_out, not_73_out, not_74_out,
       not_75_out, not_76_out, not_77_out, not_78_out, not_79_out, not_80_out, not_81_out, not_82_out,
       not_83_out, not_84_out, not_85_out, not_86_out, not_87_out, not_88_out, not_89_out, not_90_out,
       not_91_out, not_92_out, not_93_out, not_94_out, not_95_out, not_96_out, not_97_out, not_98_out,
       not_99_out, not_100_out, not_101_out, not_102_out, not_103_out;

  not not_1 (not_1_out, UC5);
  not not_2 (not_2_out, UC4);
  not not_3 (not_3_out, UC3);
  not not_4 (not_4_out, UC2);
  not not_5 (not_5_out, UC1);
  not not_6 (not_6_out, UC0);
  not not_7 (not_7_out, UC5);
  not not_8 (not_8_out, UC4);
  not not_9 (not_9_out, UC3);
  not not_10 (not_10_out, UC0);
  not not_11 (not_11_out, UC5);
  not not_12 (not_12_out, UC4);
  not not_13 (not_13_out, UC3);
  not not_14 (not_14_out, UC1);
  not not_15 (not_15_out, UC5);
  not not_16 (not_16_out, UC4);
  not not_17 (not_17_out, UC3);
  not not_18 (not_18_out, UC3);
  not not_19 (not_19_out, UC0);
  not not_20 (not_20_out, UC1);
  not not_21 (not_21_out, UC0);
  not not_22 (not_22_out, UC0);
  not not_23 (not_23_out, UC0);
  not not_24 (not_24_out, UC2);
  not not_25 (not_25_out, UC1);
  not not_26 (not_26_out, UC2);
  not not_27 (not_27_out, UC2);
  not not_28 (not_28_out, UC2);
  not not_29 (not_29_out, UC5);
  not not_30 (not_30_out, UC4);
  not not_31 (not_31_out, UC2);
  not not_32 (not_32_out, UC0);
  not not_33 (not_33_out, UC5);
  not not_34 (not_34_out, UC4);
  not not_35 (not_35_out, UC3);
  not not_36 (not_36_out, UC2);
  not not_37 (not_37_out, UC5);
  not not_38 (not_38_out, UC4);
  not not_39 (not_39_out, UC3);
  not not_40 (not_40_out, UC2);
  not not_41 (not_41_out, UC5);
  not not_42 (not_42_out, UC4);
  not not_43 (not_43_out, UC3);
  not not_44 (not_44_out, UC5);
  not not_45 (not_45_out, UC4);
  not not_46 (not_46_out, UC3);
  not not_47 (not_47_out, UC1);
  not not_48 (not_48_out, UC0);
  not not_49 (not_49_out, UC5);
  not not_50 (not_50_out, UC4);
  not not_51 (not_51_out, UC2);
  not not_52 (not_52_out, UC0);
  not not_53 (not_53_out, UC5);
  not not_54 (not_54_out, UC4);
  not not_55 (not_55_out, UC2);
  not not_56 (not_56_out, UC1);
  not not_57 (not_57_out, UC0);
  not not_58 (not_58_out, UC5);
  not not_59 (not_59_out, UC4);
  not not_60 (not_60_out, UC3);
  not not_61 (not_61_out, UC2);
  not not_62 (not_62_out, UC5);
  not not_63 (not_63_out, UC4);
  not not_64 (not_64_out, UC3);
  not not_65 (not_65_out, UC2);
  not not_66 (not_66_out, UC5);
  not not_67 (not_67_out, UC4);
  not not_68 (not_68_out, UC3);
  not not_69 (not_69_out, UC5);
  not not_70 (not_70_out, UC4);
  not not_71 (not_71_out, UC3);
  not not_72 (not_72_out, UC1);
  not not_73 (not_73_out, UC0);
  not not_74 (not_74_out, UC5);
  not not_75 (not_75_out, UC4);
  not not_76 (not_76_out, UC2);
  not not_77 (not_77_out, UC0);
  not not_78 (not_78_out, UC5);
  not not_79 (not_79_out, UC4);
  not not_80 (not_80_out, UC2);
  not not_81 (not_81_out, UC1);
  not not_82 (not_82_out, UC5);
  not not_83 (not_83_out, UC4);
  not not_84 (not_84_out, UC2);
  not not_85 (not_85_out, UC5);
  not not_86 (not_86_out, UC4);
  not not_87 (not_87_out, UC1);
  not not_88 (not_88_out, UC0);
  not not_89 (not_89_out, UC5);
  not not_90 (not_90_out, UC4);
  not not_91 (not_91_out, UC3);
  not not_92 (not_92_out, UC2);
  not not_93 (not_93_out, UC5);
  not not_94 (not_94_out, UC4);
  not not_95 (not_95_out, UC2);
  not not_96 (not_96_out, UC0);
  not not_97 (not_97_out, UC5);
  not not_98 (not_98_out, UC4);
  not not_99 (not_99_out, UC3);
  not not_100 (not_100_out, UC5);
  not not_101 (not_101_out, UC4);
  not not_102 (not_102_out, UC1);
  not not_103 (not_103_out, UC0);
  and and_1 (REGDEST, not_1_out, not_2_out, not_3_out, not_4_out, not_5_out, not_6_out);
  and and_2 (JUMP, not_7_out, not_8_out, not_9_out, UC2, UC1, not_10_out);
  and and_3 (BEQ, not_11_out, not_12_out, not_13_out, UC2, not_14_out, UC0);
  and and_4 (MEMTOREG, not_15_out, not_16_out, not_17_out, UC2, UC1, UC0);
  and and_5 (and_5_out, not_18_out, UC1, not_19_out);
  and and_6 (and_6_out, UC2, not_20_out);
  and and_7 (and_7_out, UC2, not_21_out);
  and and_8 (and_8_out, UC1, not_22_out);
  and and_9 (and_9_out, UC1, not_23_out);
  and and_10 (and_10_out, not_24_out, UC1, UC0);
  and and_11 (and_11_out, UC2, not_25_out);
  and and_12 (and_12_out, UC3, not_26_out, UC1);
  and and_13 (and_13_out, UC4, not_27_out, UC1);
  and and_14 (and_14_out, UC5, not_28_out, UC1);
  and and_15 (ULA0P2, not_29_out, not_30_out, UC3, not_31_out, UC1, not_32_out);
  and and_16 (and_16_out, not_33_out, not_34_out, not_35_out, not_36_out, UC0);
  and and_17 (and_17_out, not_37_out, not_38_out, not_39_out, not_40_out, UC1);
  and and_18 (and_18_out, not_41_out, not_42_out, not_43_out, UC1, UC0);
  and and_19 (and_19_out, not_44_out, not_45_out, not_46_out, UC2, not_47_out, not_48_out);
  and and_20 (and_20_out, not_49_out, not_50_out, UC3, not_51_out, not_52_out);
  and and_21 (MEM_WR, not_53_out, not_54_out, UC3, not_55_out, not_56_out, not_57_out);
  and and_22 (and_22_out, not_58_out, not_59_out, not_60_out, not_61_out, UC0);
  and and_23 (and_23_out, not_62_out, not_63_out, not_64_out, not_65_out, UC1);
  and and_24 (and_24_out, not_66_out, not_67_out, not_68_out, UC1, UC0);
  and and_25 (and_25_out, not_69_out, not_70_out, not_71_out, UC2, not_72_out, not_73_out);
  and and_26 (and_26_out, not_74_out, not_75_out, UC3, not_76_out, not_77_out);
  and and_27 (BNE, not_78_out, not_79_out, UC3, not_80_out, not_81_out, UC0);
  and and_28 (JR, not_82_out, not_83_out, UC3, not_84_out, UC1, UC0);
  and and_29 (JAL, not_85_out, not_86_out, UC3, UC2, not_87_out, not_88_out);
  and and_30 (and_30_out, not_89_out, not_90_out, not_91_out, not_92_out);
  and and_31 (and_31_out, not_93_out, not_94_out, not_95_out, UC1, not_96_out);
  and and_32 (and_32_out, not_97_out, not_98_out, not_99_out, UC1, UC0);
  and and_33 (and_33_out, not_100_out, not_101_out, UC2, not_102_out, not_103_out);
  or or_1 (ULA0P0, and_5_out, and_6_out, and_7_out, and_8_out, and_9_out);
  or or_2 (ULA0P1, and_10_out, and_11_out, and_12_out, and_13_out, and_14_out);
  or or_3 (ULAOPSRC, and_16_out, and_17_out, and_18_out, and_19_out, and_20_out);
  or or_4 (ULASRC, and_22_out, and_23_out, and_24_out, and_25_out, and_26_out);
  or or_5 (WE, and_30_out, and_31_out, and_32_out, and_33_out);
endmodule

// UC
module UC_W (
  input  [5:0] in_1,
  output REGDEST,
  output JUMP,
  output BEQ,
  output MEMTOREG,
  output [3:0] ALUOP,
  output MEMWRITE,
  output ALUSRC,
  output BNE,
  output JR,
  output JAL,
  output REGWRITE
);

  UC uc_1 (
    .UC5(in_1[5]), .UC4(in_1[4]), .REGDEST(REGDEST), .UC3(in_1[3]), .UC2(in_1[2]), .UC1(in_1[1]),
    .JUMP(JUMP), .UC0(in_1[0]), .BEQ(BEQ), .MEMTOREG(MEMTOREG), .ULA0P0(ALUOP[0]), .ULA0P1(ALUOP[1]),
    .ULA0P2(ALUOP[2]), .ULAOPSRC(ALUOP[3]), .MEM_WR(MEMWRITE), .ULASRC(ALUSRC), .BNE(BNE), .JR(JR),
    .JAL(JAL), .WE(REGWRITE));
endmodule

// ALUCONTROL
module ALU_CONTROL (
  input  [5:0] in_1,
  input  [3:0] in_2,
  output [5:0] out_3
);

  wire [5:0] bit_extender_1_out;

  assign bit_extender_1_out = {{3{1'b0}}, in_2[2:0]};  // Bit_Extender bit_extender_1
  Multiplexer #(.width(6), .enable("false")) multiplexer_1 (
    .in0(in_1), .in1(bit_extender_1_out), .out(out_3), .sel(in_2[3]));
endmodule

module REG_IF_ID (
  input  stall,
  input  [31:0] in_2,
  input  [31:0] in_3,
  input  CLK,
  output [31:0] out_5,
  output [31:0] out_6
);

  wire not_1_out;

  not not_1 (not_1_out, stall);
  Register #(.width(32)) register_1 (.D(in_2), .en(not_1_out), .Q(out_5), .clk(CLK));  // open: clr
  Register #(.width(32)) register_2 (.D(in_3), .en(not_1_out), .Q(out_6), .clk(CLK));  // open: clr
endmodule

module REG_ID_EX (
  input  JAL,
  input  JR,
  input  BNE,
  input  [25:0] JUMP,
  input  JUMP_2,
  input  [4:0] SHAMT,
  input  RegDest,
  input  BEQ,
  input  MemtoReg,
  input  [3:0] ALUOp,
  input  MemWrite,
  input  ALUSrc,
  input  RegWrite,
  input  [31:0] PC_4,
  input  [31:0] DATA_RS,
  input  [31:0] DATA_RT,
  input  [31:0] IMEXT,
  input  [4:0] RT,
  input  [4:0] RD,
  input  [4:0] RS,
  input  CLK,
  output JAL_2,
  output JR_2,
  output BNE_2,
  output [25:0] JUMP_3,
  output JUMP_4,
  output [4:0] SHAMT_2,
  output RegDest_2,
  output Branch,
  output MemtoReg_2,
  output [3:0] ALUOp_2,
  output MemWrite_2,
  output ALUSrc_2,
  output RegWrite_2,
  output [31:0] PC_4_2,
  output [31:0] DATA_RS_2,
  output [31:0] DATA_RT_2,
  output [31:0] IMEXT_2,
  output [4:0] RT_2,
  output [4:0] RD_2,
  output [4:0] RS_2
);

  Register #(.width(1)) register_1 (.D(JAL), .Q(JAL_2), .clk(CLK));  // open: en, clr
  Register #(.width(1)) register_2 (.D(JR), .Q(JR_2), .clk(CLK));  // open: en, clr
  Register #(.width(1)) register_3 (.D(BNE), .Q(BNE_2), .clk(CLK));  // open: en, clr
  Register #(.width(26)) register_4 (.D(JUMP), .Q(JUMP_3), .clk(CLK));  // open: en, clr
  Register #(.width(1)) register_5 (.D(JUMP_2), .Q(JUMP_4), .clk(CLK));  // open: en, clr
  Register #(.width(5)) register_6 (.D(SHAMT), .Q(SHAMT_2), .clk(CLK));  // open: en, clr
  Register #(.width(1)) register_7 (.D(RegDest), .Q(RegDest_2), .clk(CLK));  // open: en, clr
  Register #(.width(1)) register_8 (.D(BEQ), .Q(Branch), .clk(CLK));  // open: en, clr
  Register #(.width(1)) register_9 (.D(MemtoReg), .Q(MemtoReg_2), .clk(CLK));  // open: en, clr
  Register #(.width(4)) register_10 (.D(ALUOp), .Q(ALUOp_2), .clk(CLK));  // open: en, clr
  Register #(.width(1)) register_11 (.D(MemWrite), .Q(MemWrite_2), .clk(CLK));  // open: en, clr
  Register #(.width(1)) register_12 (.D(ALUSrc), .Q(ALUSrc_2), .clk(CLK));  // open: en, clr
  Register #(.width(1)) register_13 (.D(RegWrite), .Q(RegWrite_2), .clk(CLK));  // open: en, clr
  Register #(.width(32)) register_14 (.D(PC_4), .Q(PC_4_2), .clk(CLK));  // open: en, clr
  Register #(.width(32)) register_15 (.D(DATA_RS), .Q(DATA_RS_2), .clk(CLK));  // open: en, clr
  Register #(.width(32)) register_16 (.D(DATA_RT), .Q(DATA_RT_2), .clk(CLK));  // open: en, clr
  Register #(.width(32)) register_17 (.D(IMEXT), .Q(IMEXT_2), .clk(CLK));  // open: en, clr
  Register #(.width(5)) register_18 (.D(RT), .Q(RT_2), .clk(CLK));  // open: en, clr
  Register #(.width(5)) register_19 (.D(RD), .Q(RD_2), .clk(CLK));  // open: en, clr
  Register #(.width(5)) register_20 (.D(RS), .Q(RS_2), .clk(CLK));  // open: en, clr
endmodule

module REG_EX_MEM (
  input  [31:0] BR_RS,
  input  [31:0] PC_4,
  input  JAL,
  input  JR,
  input  BNE,
  input  JUMP,
  input  [31:0] JUMP_ADDRESS,
  input  BEQ,
  input  MEMTOREG,
  input  MEMORY_WRITE,
  input  REGWRITE,
  input  [31:0] BRANCH_ADDRESS,
  input  zero,
  input  [31:0] ALU_OUT,
  input  [31:0] DATA_RT,
  input  [4:0] WRITE_REGISTER,
  input  [4:0] RT,
  input  CLK,
  output [31:0] BR_RS_2,
  output [31:0] JUMP_ADDRESS_2,
  output JAL_2,
  output JR_2,
  output BNE_2,
  output JUMP_2,
  output [31:0] JUMP_ADDRESS_3,
  output BEQ_2,
  output MEMTOREG_2,
  output MEMORY_WRITE_2,
  output REGWRITE_2,
  output [31:0] BRANCH_ADDRESS_2,
  output zero_2,
  output [31:0] ALU_OUT_2,
  output [31:0] DATA_RT_2,
  output [4:0] WRITE_REGISTER_2,
  output [4:0] RT_2
);

  Register #(.width(5)) register_1 (.D(RT), .Q(RT_2), .clk(CLK));  // open: en, clr
  Register #(.width(32)) register_2 (.D(BR_RS), .Q(BR_RS_2), .clk(CLK));  // open: en, clr
  Register #(.width(32)) register_3 (.D(PC_4), .Q(JUMP_ADDRESS_2), .clk(CLK));  // open: en, clr
  Register #(.width(1)) register_4 (.D(JAL), .Q(JAL_2), .clk(CLK));  // open: en, clr
  Register #(.width(1)) register_5 (.D(JR), .Q(JR_2), .clk(CLK));  // open: en, clr
  Register #(.width(1)) register_6 (.D(BNE), .Q(BNE_2), .clk(CLK));  // open: en, clr
  Register #(.width(1)) register_7 (.D(JUMP), .Q(JUMP_2), .clk(CLK));  // open: en, clr
  Register #(.width(32)) register_8 (.D(JUMP_ADDRESS), .Q(JUMP_ADDRESS_3), .clk(CLK));  // open: en, clr
  Register #(.width(1)) register_9 (.D(BEQ), .Q(BEQ_2), .clk(CLK));  // open: en, clr
  Register #(.width(1)) register_10 (.D(MEMTOREG), .Q(MEMTOREG_2), .clk(CLK));  // open: en, clr
  Register #(.width(1)) register_11 (.D(MEMORY_WRITE), .Q(MEMORY_WRITE_2), .clk(CLK));  // open: en, clr
  Register #(.width(1)) register_12 (.D(REGWRITE), .Q(REGWRITE_2), .clk(CLK));  // open: en, clr
  Register #(.width(32)) register_13 (.D(BRANCH_ADDRESS), .Q(BRANCH_ADDRESS_2), .clk(CLK));  // open: en, clr
  Register #(.width(1)) register_14 (.D(zero), .Q(zero_2), .clk(CLK));  // open: en, clr
  Register #(.width(32)) register_15 (.D(ALU_OUT), .Q(ALU_OUT_2), .clk(CLK));  // open: en, clr
  Register #(.width(32)) register_16 (.D(DATA_RT), .Q(DATA_RT_2), .clk(CLK));  // open: en, clr
  Register #(.width(5)) register_17 (.D(WRITE_REGISTER), .Q(WRITE_REGISTER_2), .clk(CLK));  // open: en, clr
endmodule

module REG_MEM_WB (
  input  JAL,
  input  [31:0] PC_4,
  input  REG_WRITE,
  input  MEMTOREG,
  input  [31:0] MEM_OUT,
  input  [31:0] ALU_OUT,
  input  [4:0] WRITE_REGISTER,
  input  CLK,
  output JAL_2,
  output [31:0] PC_4_2,
  output REG_WRITE_2,
  output MEMTOREG_2,
  output [31:0] MEM_OUT_2,
  output [31:0] ALU_OUT_2,
  output [4:0] WRITE_REGISTER_2
);

  Register #(.width(1)) register_1 (.D(JAL), .Q(JAL_2), .clk(CLK));  // open: en, clr
  Register #(.width(32)) register_2 (.D(PC_4), .Q(PC_4_2), .clk(CLK));  // open: en, clr
  Register #(.width(1)) register_3 (.D(REG_WRITE), .Q(REG_WRITE_2), .clk(CLK));  // open: en, clr
  Register #(.width(1)) register_4 (.D(MEMTOREG), .Q(MEMTOREG_2), .clk(CLK));  // open: en, clr
  Register #(.width(32)) register_5 (.D(MEM_OUT), .Q(MEM_OUT_2), .clk(CLK));  // open: en, clr
  Register #(.width(32)) register_6 (.D(ALU_OUT), .Q(ALU_OUT_2), .clk(CLK));  // open: en, clr
  Register #(.width(5)) register_7 (.D(WRITE_REGISTER), .Q(WRITE_REGISTER_2), .clk(CLK));  // open: en, clr
endmodule

module fowarding (
  input  ex_mem_writeReg,
  input  [4:0] ex_mem_RegDd,
  input  [4:0] id_ex_RegRs,
  input  [4:0] ex_mem_RegRt,
  input  mem_wb_writeReg,
  input  [4:0] mem_wb_RegDd,
  input  [4:0] id_ex_RegRt,
  output [1:0] FA,
  output fsw,
  output [1:0] FB
);

  wire and_5_out, and_6_out, comparator_1_eq, comparator_2_eq, comparator_3_eq, comparator_4_eq,
       comparator_5_eq, comparator_6_eq, comparator_7_eq, comparator_8_eq, not_1_out, not_2_out, not_3_out,
       not_4_out;

  not not_1 (not_1_out, comparator_1_eq);
  Comparator #(.width(5)) comparator_1 (.a(ex_mem_RegDd), .b({5{1'b0}}), .eq(comparator_1_eq));  // open: gt, lt
  Comparator #(.width(5)) comparator_2 (.a(ex_mem_RegDd), .b(id_ex_RegRs), .eq(comparator_2_eq));  // open: gt, lt
  not not_2 (not_2_out, comparator_3_eq);
  Comparator #(.width(5)) comparator_3 (.a(mem_wb_RegDd), .b({5{1'b0}}), .eq(comparator_3_eq));  // open: gt, lt
  Comparator #(.width(5)) comparator_4 (.a(mem_wb_RegDd), .b(id_ex_RegRs), .eq(comparator_4_eq));  // open: gt, lt
  Comparator #(.width(5)) comparator_5 (.a(id_ex_RegRt), .b(ex_mem_RegDd), .eq(comparator_5_eq));  // open: gt, lt
  Comparator #(.width(5)) comparator_6 (.a(mem_wb_RegDd), .b(id_ex_RegRt), .eq(comparator_6_eq));  // open: gt, lt
  and and_1 (FA[1], ex_mem_writeReg, not_1_out, comparator_2_eq);
  and and_2 (FA[0], mem_wb_writeReg, and_5_out, not_2_out, comparator_4_eq);
  and and_3 (FB[1], mem_wb_writeReg, not_1_out, comparator_5_eq);
  and and_4 (FB[0], and_6_out, comparator_6_eq, mem_wb_writeReg, not_2_out);
  not not_3 (not_3_out, comparator_2_eq);
  not not_4 (not_4_out, comparator_7_eq);
  Comparator #(.width(5)) comparator_7 (.a(ex_mem_RegDd), .b(id_ex_RegRt), .eq(comparator_7_eq));  // open: gt, lt
  and and_5 (and_5_out, ex_mem_writeReg, not_1_out, not_3_out);
  and and_6 (and_6_out, ex_mem_writeReg, not_1_out, not_4_out);
  Comparator #(.width(5)) comparator_8 (.a(ex_mem_RegRt), .b(mem_wb_RegDd), .eq(comparator_8_eq));  // open: gt, lt
  and and_7 (fsw, comparator_8_eq, mem_wb_writeReg);
endmodule

module hazard_unit (
  input  id_ex_readmem,
  input  [4:0] id_ex_regRt,
  input  [4:0] if_id_regRs,
  input  [4:0] if_id_regRt,
  input  [5:0] opcode,
  output stall
);

  wire and_1_out, comparator_1_eq, comparator_2_eq, comparator_3_eq, not_1_out, or_1_out;

  Comparator #(.width(5)) comparator_1 (.a(id_ex_regRt), .b(if_id_regRs), .eq(comparator_1_eq));  // open: gt, lt
  Comparator #(.width(5)) comparator_2 (.a(id_ex_regRt), .b(if_id_regRt), .eq(comparator_2_eq));  // open: gt, lt
  not not_1 (not_1_out, comparator_3_eq);
  Comparator #(.width(6)) comparator_3 (.a(opcode), .b(6'b001000), .eq(comparator_3_eq));  // open: gt, lt
  and and_1 (and_1_out, comparator_2_eq, not_1_out);
  or or_1 (or_1_out, comparator_1_eq, and_1_out);
  and and_2 (stall, id_ex_readmem, or_1_out);
endmodule

module jal (
  output JR,
  output JAL,
  output WE
);

  wire and_3_out, and_4_out, and_5_out, and_6_out, not_1_out, not_2_out, not_3_out, not_4_out, not_5_out,
       not_6_out, not_7_out, not_8_out, not_9_out, not_10_out, not_11_out, not_12_out, not_13_out,
       not_14_out, not_15_out, not_16_out, not_17_out, not_18_out, not_19_out, not_20_out, not_21_out,
       not_22_out, undriven, undriven_2, undriven_3, undriven_4, undriven_5, undriven_6, undriven_7,
       undriven_8, undriven_9, undriven_10, undriven_11, undriven_12, undriven_13, undriven_14, undriven_15,
       undriven_16, undriven_17, undriven_18;

  not not_1 (not_1_out, undriven);
  not not_2 (not_2_out, undriven_2);
  not not_3 (not_3_out, undriven_8);
  not not_4 (not_4_out, undriven_3);
  not not_5 (not_5_out, undriven_6);
  not not_6 (not_6_out, undriven_14);
  not not_7 (not_7_out, undriven_16);
  not not_8 (not_8_out, undriven_4);
  not not_9 (not_9_out, undriven_7);
  not not_10 (not_10_out, undriven_10);
  not not_11 (not_11_out, undriven_13);
  not not_12 (not_12_out, undriven_4);
  not not_13 (not_13_out, undriven_7);
  not not_14 (not_14_out, undriven_13);
  not not_15 (not_15_out, undriven_17);
  not not_16 (not_16_out, undriven_4);
  not not_17 (not_17_out, undriven_7);
  not not_18 (not_18_out, undriven_10);
  not not_19 (not_19_out, undriven_4);
  not not_20 (not_20_out, undriven_7);
  not not_21 (not_21_out, undriven_15);
  not not_22 (not_22_out, undriven_17);
  and and_1 (JR, not_1_out, not_2_out, undriven_5, not_3_out, undriven_11, undriven_18);
  and and_2 (JAL, not_4_out, not_5_out, undriven_9, undriven_12, not_6_out, not_7_out);
  and and_3 (and_3_out, not_8_out, not_9_out, not_10_out, not_11_out);
  and and_4 (and_4_out, not_12_out, not_13_out, not_14_out, undriven_15, not_15_out);
  and and_5 (and_5_out, not_16_out, not_17_out, not_18_out, undriven_15, undriven_17);
  and and_6 (and_6_out, not_19_out, not_20_out, undriven_13, not_21_out, not_22_out);
  or or_1 (WE, and_3_out, and_4_out, and_5_out, and_6_out);
endmodule
